// Logisim project HW3.circ as structural Verilog
module cpu_main (
  input  in_1,
  input  in_2,
  input  in_3,
  input  in_4,
  output [3:0] out_5,
  output [2:0] out_6,
  output [4:0] out_7
);

  wire and_1_out, clock_1_out, control_1_shut_down_halt, not_1_out;
  wire [15:0] adder_1_out, register_1_q;
  wire [15:5] ram_1_data;

  Clock clock_1 (.out(clock_1_out));
  and and_1 (and_1_out, clock_1_out, not_1_out);
  not not_1 (not_1_out, control_1_shut_down_halt);
  Register #(.width(16)) register_1 (.D(adder_1_out), .en(1'b1), .Q(register_1_q), .clk(and_1_out));  // open: clr
  Adder #(.width(16)) adder_1 (.a(16'h1), .b(register_1_q), .out(adder_1_out));  // open: cin, cout
  RAM #(.addrWidth(16), .dataWidth(16), .bus("separate")) ram_1 (
    .addr(register_1_q), .data({ram_1_data, out_6, out_7[1:0]}), .sel(1'b1), .ld(1'b1));  // open: din, str, clk, clr
  control control_1 (.opcode(ram_1_data[15:11]), .shut_down_halt(control_1_shut_down_halt));
  register register_2 ();  // open: allow_write, Write_Register_which_reg, reset, Register_Data_data_input, clock_update_reg_per_clock, data_1, data_2, Read_Regisiter2, Read_Regisiter1
  ALU_q1_q2 alu_q1_q2_1 (.opcode_decide_which_instrusion_would_be_selected(ram_1_data[15:11]));  // open: op1, op2, data_output
  RAM #(.addrWidth(16), .dataWidth(16)) ram_2 ();  // open: addr, data, sel, clk, ld, clr

  assign out_5 = {in_4, in_3, in_2, in_1};
  assign out_7[4:2] = out_6;

  // Other names for the same wires on the sheet: debug_ime[4:0] = {out_6, out_7[1:0]}; debug_r2[2:0] = out_6

  // Notes on the sheet:
  //   呢個input遲d連halt instrusion
  //   debug area
  //   for R type
  //   for I type
endmodule

module ALU_q1_q2 (
  input  [15:0] op1,
  input  [15:0] op2,
  input  [4:0] opcode_decide_which_instrusion_would_be_selected,
  output [15:0] data_output
);

  wire [15:0] adder_1_out, and_1_out, multiplier_1_out, negator_1_out, or_1_out;

  Adder #(.width(16)) adder_1 (.a(op1), .b(op2), .out(adder_1_out));  // open: cin, cout
  Negator #(.width(16)) negator_1 (.in(op1), .out(negator_1_out));
  assign and_1_out = op1 & op2;  // AND_Gate and_1, 16 bits wide
  assign or_1_out = op1 | op2;  // OR_Gate or_1, 16 bits wide
  Multiplier #(.width(16)) multiplier_1 (.a(op1), .b(op2), .out(multiplier_1_out));  // open: cin, cout
  Multiplexer #(.select(5), .width(16)) multiplexer_1 (
    .in1(adder_1_out), .in2(negator_1_out), .in5(and_1_out), .in6(or_1_out), .in7(multiplier_1_out),
    .out(data_output), .sel(opcode_decide_which_instrusion_would_be_selected), .en(1'b1));  // open: in0, in3, in4, in8, in9, in10, in11, in12, in13, in14, in15, in16, in17, in18, in19, in20, in21, in22, in23, in24, in25, in26, in27, in28, in29, in30, in31

  // Notes on the sheet:
  //   1.li
  //   2.add
  //   3.neg
  //   4.ble
  //   5.halt
  //   6.and
  //   7.or
  //   8.mult
  //   9.load
  //   10.store
  //   11.move
endmodule

module register (
  input  allow_write,
  input  [2:0] Read_Regisiter1,
  input  [2:0] Write_Register_which_reg,
  input  [2:0] Read_Regisiter2,
  input  reset,
  input  [15:0] Register_Data_data_input,
  input  clock_update_reg_per_clock,
  output [15:0] data_1,
  output [15:0] data_2
);

  wire and_1_out, and_2_out, and_3_out, and_4_out, and_5_out, and_6_out, and_7_out, and_8_out,
       decoder_1_out0, decoder_1_out1, decoder_1_out2, decoder_1_out3, decoder_1_out4, decoder_1_out5,
       decoder_1_out6, decoder_1_out7;
  wire [15:0] register_1_q, register_2_q, register_3_q, register_4_q, register_5_q, register_6_q,
       register_7_q, register_8_q;

  Decoder #(.select(3), .enable("false")) decoder_1 (
    .out0(decoder_1_out0), .out1(decoder_1_out1), .out2(decoder_1_out2), .out3(decoder_1_out3),
    .out4(decoder_1_out4), .out5(decoder_1_out5), .out6(decoder_1_out6), .out7(decoder_1_out7),
    .sel(Write_Register_which_reg));
  and and_1 (and_1_out, allow_write, decoder_1_out0);
  and and_2 (and_2_out, allow_write, decoder_1_out1);
  and and_3 (and_3_out, allow_write, decoder_1_out2);
  and and_4 (and_4_out, allow_write, decoder_1_out3);
  and and_5 (and_5_out, allow_write, decoder_1_out4);
  and and_6 (and_6_out, allow_write, decoder_1_out5);
  and and_7 (and_7_out, allow_write, decoder_1_out6);
  and and_8 (and_8_out, allow_write, decoder_1_out7);
  Register #(.width(16)) register_1 (
    .D(Register_Data_data_input), .en(and_1_out), .Q(register_1_q), .clk(clock_update_reg_per_clock),
    .clr(reset));
  Register #(.width(16)) register_2 (
    .D(Register_Data_data_input), .en(and_2_out), .Q(register_2_q), .clk(clock_update_reg_per_clock),
    .clr(reset));
  Register #(.width(16)) register_3 (
    .D(Register_Data_data_input), .en(and_3_out), .Q(register_3_q), .clk(clock_update_reg_per_clock),
    .clr(reset));
  Register #(.width(16)) register_4 (
    .D(Register_Data_data_input), .en(and_4_out), .Q(register_4_q), .clk(clock_update_reg_per_clock),
    .clr(reset));
  Register #(.width(16)) register_5 (
    .D(Register_Data_data_input), .en(and_5_out), .Q(register_5_q), .clk(clock_update_reg_per_clock),
    .clr(reset));
  Register #(.width(16)) register_6 (
    .D(Register_Data_data_input), .en(and_6_out), .Q(register_6_q), .clk(clock_update_reg_per_clock),
    .clr(reset));
  Register #(.width(16)) register_7 (
    .D(Register_Data_data_input), .en(and_7_out), .Q(register_7_q), .clk(clock_update_reg_per_clock),
    .clr(reset));
  Register #(.width(16)) register_8 (
    .D(Register_Data_data_input), .en(and_8_out), .Q(register_8_q), .clk(clock_update_reg_per_clock),
    .clr(reset));
  Multiplexer #(.select(3), .width(16), .enable("false")) multiplexer_1 (
    .in0(register_1_q), .in1(register_2_q), .in2(register_3_q), .in3(register_4_q), .in4(register_5_q),
    .in5(register_6_q), .in6(register_7_q), .in7(register_8_q), .out(data_1), .sel(Read_Regisiter1));
  Multiplexer #(.select(3), .width(16), .enable("false")) multiplexer_2 (
    .in0(register_1_q), .in1(register_2_q), .in2(register_3_q), .in3(register_4_q), .in4(register_5_q),
    .in5(register_6_q), .in6(register_7_q), .in7(register_8_q), .out(data_2), .sel(Read_Regisiter2));
endmodule

module control (
  input  [4:0] opcode,
  output shut_down_halt
);

  wire _1_out, _2_out, _3_out, _4_out, _6_out, _7_out, _8_out, _9_out, _10_out, _11_out, _12_out, _13_out,
       _14_out, _15_out, _16_out;

  and _1 (_1_out, ~opcode[4], ~opcode[3], ~opcode[2], ~opcode[1], ~opcode[0]);  // AND_Gate
  and _2 (_2_out, ~opcode[4], ~opcode[3], ~opcode[2], ~opcode[1], opcode[0]);  // AND_Gate
  and _3 (_3_out, ~opcode[4], ~opcode[3], ~opcode[2], opcode[1], ~opcode[0]);  // AND_Gate
  and _4 (_4_out, ~opcode[4], ~opcode[3], ~opcode[2], opcode[1], opcode[0]);  // AND_Gate
  and _5 (shut_down_halt, ~opcode[4], ~opcode[3], opcode[2], ~opcode[1], ~opcode[0]);  // AND_Gate
  and _6 (_6_out, ~opcode[4], ~opcode[3], opcode[2], ~opcode[1], opcode[0]);  // AND_Gate
  and _7 (_7_out, ~opcode[4], ~opcode[3], opcode[2], opcode[1], ~opcode[0]);  // AND_Gate
  and _8 (_8_out, ~opcode[4], ~opcode[3], opcode[2], opcode[1], opcode[0]);  // AND_Gate
  and _9 (_9_out, ~opcode[4], opcode[3], ~opcode[2], ~opcode[1], ~opcode[0]);  // AND_Gate
  and _10 (_10_out, ~opcode[4], opcode[3], ~opcode[2], ~opcode[1], opcode[0]);  // AND_Gate
  and _11 (_11_out, ~opcode[4], opcode[3], ~opcode[2], opcode[1], ~opcode[0]);  // AND_Gate
  and _12 (_12_out, ~opcode[4], opcode[3], ~opcode[2], opcode[1], opcode[0]);  // AND_Gate
  and _13 (_13_out, ~opcode[4], opcode[3], opcode[2], ~opcode[1], ~opcode[0]);  // AND_Gate
  and _14 (_14_out, ~opcode[4], opcode[3], opcode[2], ~opcode[1], opcode[0]);  // AND_Gate
  and _15 (_15_out, ~opcode[4], opcode[3], opcode[2], opcode[1], ~opcode[0]);  // AND_Gate
  and _16 (_16_out, ~opcode[4], opcode[3], opcode[2], opcode[1], opcode[0]);  // AND_Gate

  // Other names for the same wires on the sheet: _0 = opcode[0]; _1 = opcode[1]; _2 = opcode[2]; _3 = opcode[3];
  //   _4 = opcode[4]

  // Notes on the sheet:
  //   1.li
  //   2.add
  //   3.neg
  //   4.ble
  //   5.halt
  //   6.and
  //   7.or
  //   8.mult
  //   9.load
  //   10.store
  //   11.move
endmodule
